// Logisim project C3_top_JoseAlas.circ as structural Verilog: 8 circuits, main circuit main
module main (
  input  ON_OFF,
  input  Sens_Envase,
  input  Sens_Nivel,
  input  Sens_Sello,
  input  CLK,
  output Motor_Cinta,
  output Valvula,
  output Actuador_Sello
);

  wire Enable_Fill, Fill_Done;

  Clock clock_1 ();  // open: out
  fsm1_block fsm1_block_1 (
    .O(ON_OFF), .E(Sens_Envase), .F(Fill_Done), .S(Sens_Sello), .CLK(CLK), .Motor_Cinta(Motor_Cinta),
    .Actuador(Actuador_Sello), .Enable_Fill(Enable_Fill));
  fsm2_block fsm2_block_1 (.EN(Enable_Fill), .N(Sens_Nivel), .CLK(CLK), .Valvula(Valvula), .Fill_Done(Fill_Done));
endmodule

module fsm1_next_state (
  input  S1,
  input  S0,
  input  O,
  input  E,
  input  F,
  input  S,
  output S1_next,
  output S0_next
);

  wire and_1_out, and_2_out, and_3_out, and_4_out, and_5_out, and_6_out, and_7_out, not_1_out, not_2_out,
       not_3_out, not_4_out, or_1_out, or_2_out;

  not not_1 (not_1_out, S1);
  not not_2 (not_2_out, S0);
  not not_3 (not_3_out, E);
  not not_4 (not_4_out, S);
  and and_1 (and_1_out, not_1_out, S0, E);
  and and_2 (and_2_out, S1, not_2_out);
  and and_3 (and_3_out, S1, S0, not_4_out);
  and and_4 (and_4_out, not_1_out, not_2_out);
  and and_5 (and_5_out, not_1_out, S0, not_3_out);
  and and_6 (and_6_out, S1, not_2_out, F);
  and and_7 (and_7_out, S1, S0);
  or or_1 (or_1_out, and_1_out, and_2_out, and_3_out);
  or or_2 (or_2_out, and_4_out, and_5_out, and_6_out, and_7_out);
  and and_8 (S1_next, O, or_1_out);
  and and_9 (S0_next, O, or_2_out);
endmodule

module fsm1_output (
  input  S1,
  input  S0,
  output Motor_Cinta,
  output Actuador_Sello,
  output Enable_Fill
);

  wire not_1_out, not_2_out;

  not not_1 (not_1_out, S1);
  not not_2 (not_2_out, S0);
  and and_1 (Motor_Cinta, not_1_out, S0);
  and and_2 (Actuador_Sello, S1, S0);
  and and_3 (Enable_Fill, S1, not_2_out);
endmodule

module fsm2_next_state (
  input  EN,
  input  N,
  output V0_next
);

  wire not_1_out;

  not not_1 (not_1_out, N);
  and and_1 (V0_next, EN, not_1_out);
endmodule

module fsm2_output (
  input  V0,
  input  EN,
  input  N,
  output Valvula,
  output Fill_Done
);

  wire not_1_out;

  not not_1 (not_1_out, N);
  and and_1 (Valvula, EN, not_1_out);
  and and_2 (Fill_Done, V0, N);
endmodule

module fsm1_block (
  input  O,
  input  E,
  input  F,
  input  S,
  input  CLK,
  output Motor_Cinta,
  output Actuador,
  output Enable_Fill
);

  wire fsm1_next_state_1_s0_next, fsm1_next_state_1_s1_next, S0, S1;

  fsm1_next_state fsm1_next_state_1 (
    .S1(S1), .S0(S0), .O(O), .E(E), .F(F), .S(S), .S1_next(fsm1_next_state_1_s1_next),
    .S0_next(fsm1_next_state_1_s0_next));
  D_Flip_Flop d_ff_1 (.D(fsm1_next_state_1_s0_next), .clk(CLK), .Q(S0));  // open: Qn, preset, reset
  D_Flip_Flop d_ff_2 (.D(fsm1_next_state_1_s1_next), .clk(CLK), .Q(S1));  // open: Qn, preset, reset
  fsm1_output fsm1_output_1 (
    .S1(S1), .S0(S0), .Motor_Cinta(Motor_Cinta), .Actuador_Sello(Actuador), .Enable_Fill(Enable_Fill));
endmodule

module fsm2_block (
  input  EN,
  input  N,
  input  CLK,
  output Valvula,
  output Fill_Done
);

  wire fsm2_next_state_1_v0_next, V0;

  fsm2_next_state fsm2_next_state_1 (.EN(EN), .N(N), .V0_next(fsm2_next_state_1_v0_next));
  D_Flip_Flop d_ff_1 (.D(fsm2_next_state_1_v0_next), .clk(CLK), .Q(V0));  // open: Qn, preset, reset
  fsm2_output fsm2_output_1 (.V0(V0), .EN(EN), .N(N), .Valvula(Valvula), .Fill_Done(Fill_Done));
endmodule

module TOP (
  input  in_1,
  input  in_2,
  input  in_3,
  input  in_4,
  output out_5,
  output out_6,
  output out_7
);

  wire clock_1_out;

  Clock clock_1 (.out(clock_1_out));
  main main_1 (
    .ON_OFF(in_1), .Sens_Envase(in_2), .Sens_Nivel(in_3), .Sens_Sello(in_4), .CLK(clock_1_out),
    .Motor_Cinta(out_5), .Valvula(out_6), .Actuador_Sello(out_7));
endmodule
